// Logisim project main.circ as structural Verilog: 1 circuit, main circuit main
module main (
);

  RAM ram_1 ();  // open: addr, data, sel, clk, ld, clr
  Joystick joystick_1 ();  // open: x, y
  ROM rom_1 ();  // open: addr, data, sel
endmodule
